// Digital circuit CPU.dig as structural Verilog
module CPU (
  input  CLK_RAW,
  input  [31:0] Breakpoint,
  output [31:0] x8_s0_fp,
  output [31:0] x9_s1,
  output [31:0] x10_a0,
  output [31:0] PC,
  output [31:0] Address,
  output [31:0] Instr,
  output [7:0] Data_Read,
  output [5:0] Step,
  output [7:0] Substep,
  output [16:0] out_10,
  output [15:0] out_11,
  output [31:0] A,
  output [31:0] B,
  output [31:0] Result,
  output [11:0] CSR_Address,
  output [31:0] x11_a1,
  output [31:0] x4_tp,
  output [31:0] x5_t0,
  output [31:0] x6_t1,
  output [31:0] x7_t2,
  output [31:0] x1_ra,
  output [31:0] x2_sp,
  output [31:0] x3_gp,
  output [31:0] x12_a2,
  output [31:0] x13_a3,
  output [31:0] x14_a4,
  output [31:0] x15_a5,
  output [5:0] out_29,
  output [31:0] out_30,
  output [31:0] out_31,
  output [31:0] out_32,
  output [31:0] out_33,
  output [31:0] out_34,
  output [31:0] out_35,
  output [10:0] out_36,
  output [31:0] out_37,
  output [7:0] Data_Write
);

  wire ADDR_CLK, ADDR_IN, ADDR_LATCH, ALU_A, ALU_AUX, ALU_B, ALU_N, alu_shift_step_1_p4, alu_shift_step_1_p5,
       alu_shift_step_1_p6, and_1_out, and_2_out, and_3_out, B_INSTR, B_RUN, B_STEP, B_STOP, B_SUBSTEP,
       BR_STOP, BUS_CLK, BUS_EN, BUT_STOP, button_1_out, button_2_out, CLK, clock_1_lastsubstep,
       comparator_1_eq, comparator_1_gt, comparator_1_lt, comparator_2_eq, CS_IO, CS_RAM, CS_ROM,
       CSR_ADDR_LATCH, CSR_IN, CSR_IN_LATCH, CSR_OUT, CSR_OUT_LATCH, CSR_PC_OUT, d_ff_1_q, d_ff_4_q,
       d_ff_as_1_q, d_ff_as_2_q, diodeforward_1_out, ImmB, ImmCSR, ImmI, ImmJ, ImmS, ImmU, INT1P, INT2P,
       INT3P, LASTSTEP, LEN8, MEM_IN, MEM_OUT, MEPC_OUT, MIE, mie_1_mei1e, mie_1_mei2e, mie_1_mei3e,
       mip_1_mei1p, mip_1_mei2p, mip_1_mei3p, MRET, MTVEC_OUT, multiplexer_1_out, nADDR_PE, nALU_RESET, nCLK,
       nILL_OP, nIRQ, nKB_INT, nMEM_OE, nMEM_WE, nOPDONE, not_1_out, not_2_out, not_3_out, nPC_CNT_PE,
       nREG_IN_EN, nRESET, nS_EXT, nSTEPDONE, nWAKEUP, OP_IMM_LATCH, OP_IN, OP_IN_MUX, OP_LATCH, or_1_out,
       PC_IN, PC_IN_LATCH, PC_IN_MUX, PC_OUT, PC_OUT_LATCH, PC_OUT_SnP, REG_IN, RESET, RS1, Running, SLEEP,
       TRAP_OP, TRAP_OP_SnP;
  wire [0:0] LEN;
  wire [1:0] ALU_A_MUX, REG_IN_MUX, TRAP2;
  wire [2:0] ALU_B_MUX, ALU_OP;
  wire [3:0] RSA, RSB, RSD;
  wire [7:0] DATA;
  wire [15:0] DATA_ADDR;
  wire [31:0] switch_1_b;
  wire [31:29] MicroCode_d;

  Switch #(.Bits(32)) switch_1 (.A(x3_gp), .B(switch_1_b));
  Register_view register_view_1 (
    .BUS_CLK(BUS_CLK), .nREG_IN_EN(nREG_IN_EN), .REG_IN(REG_IN), .RSD(RSD), .x1_ra(x1_ra), .x2_sp(x2_sp),
    .x3_gp(x3_gp), .x4_tp(x4_tp), .x5_t0(x5_t0), .x6_t1(x6_t1), .x7_t2(x7_t2), .x8_s0_fp(x8_s0_fp),
    .x9_s1(x9_s1), .x10_a0(x10_a0), .x11_a1(x11_a1), .x12_a2(x12_a2), .x13_a3(x13_a3), .x14_a4(x14_a4),
    .x15_a5(x15_a5));
  PullDown #(.Bits(32)) pulldown_1 (.out(switch_1_b));
  not not_1 (not_1_out, MRET);
  Button #(.activeLow("true")) button_1 (.out(button_1_out));
  Button #(.activeLow("true")) button_2 (.out(button_2_out));
  Multiplexer multiplexer_1 (.sel(out_10[13]), .in_0(RS1), .in_1(ImmCSR), .out(multiplexer_1_out));
  PullDown pulldown_2 (.out(CSR_IN));
  and and_1 (and_1_out, not_1_out, PC_IN_MUX);
  D_FF_AS #(.Default(1)) d_ff_as_1 (.Set(CLK), .D(1'b0), .C(PC_IN_MUX), .Clr(1'b0), .Q(d_ff_as_1_q));  // open: nQ
  D_FF_AS #(.Default(1)) d_ff_as_2 (.Set(CLK), .D(MRET), .C(PC_IN_MUX), .Clr(1'b0), .Q(d_ff_as_2_q));  // open: nQ
  Comparator #(.Bits(32)) comparator_1 (
    .a(switch_1_b), .b(32'h1), .gt(comparator_1_gt), .eq(comparator_1_eq), .lt(comparator_1_lt));
  LED led_1 (.in(Running));
  LED led_2 (.in(not_2_out));
  not not_2 (not_2_out, Running);
  Button #(.activeLow("true")) Stop (.out(BUT_STOP));
  Button #(.activeLow("true")) Run (.out(B_RUN));
  Button #(.activeLow("true")) One_Instruction (.out(B_INSTR));
  Button #(.activeLow("true")) One_Step (.out(B_STEP));
  Button #(.activeLow("true")) One_Substep (.out(B_SUBSTEP));
  LED led_3 (.in(comparator_1_gt));
  LED led_4 (.in(comparator_1_eq));
  Comparator #(.Bits(32)) comparator_2 (.a(Breakpoint), .b(PC), .eq(comparator_2_eq));  // open: gt, lt
  and and_2 (and_2_out, nIRQ, nILL_OP);
  MEPC mepc_1 (
    .BUS_CLK(BUS_CLK), .PC_IN(PC_OUT), .IN_EN(and_1_out), .CSR_IN(CSR_OUT), .CSR_IN_LATCH(CSR_IN_LATCH),
    .CSR_ADDR(CSR_Address), .RESET(RESET), .OUT(MEPC_OUT), .CSR_OUT(CSR_IN), .mepc(out_30));
  MTVEC mtvec_1 (
    .BUS_CLK(BUS_CLK), .MTVEC_SnP(PC_IN_MUX), .CSR_IN(CSR_OUT), .CSR_IN_LATCH(CSR_IN_LATCH),
    .CSR_ADDR(CSR_Address), .RESET(RESET), .MTVEC_OUT(MTVEC_OUT), .CSR_OUT(CSR_IN), .mtvec(out_37));
  MSCRATCH mscratch_1 (
    .BUS_CLK(BUS_CLK), .CSR_IN(CSR_OUT), .CSR_IN_LATCH(CSR_IN_LATCH), .CSR_ADDR(CSR_Address), .RESET(RESET),
    .CSR_OUT(CSR_IN), .mscratch(out_31));
  MSTATUS mstatus_1 (
    .CLK(CLK), .BUS_CLK(BUS_CLK), .CSR_IN(CSR_OUT), .CSR_IN_LATCH(CSR_IN_LATCH),
    .CSR_OUT_LATCH(CSR_OUT_LATCH), .CSR_ADDR(CSR_Address), .IRQ(PC_IN_MUX), .MRET(MRET),
    .IRQ_LATCH(d_ff_as_1_q), .RESET(RESET), .nRESET(nRESET), .CSR_OUT(CSR_IN), .mstatus(out_32), .MIE(MIE));  // open: MPIE
  MIE mie_1 (
    .CLK(CLK), .BUS_CLK(BUS_CLK), .CSR_IN(CSR_OUT), .CSR_IN_LATCH(CSR_IN_LATCH),
    .CSR_OUT_LATCH(CSR_OUT_LATCH), .CSR_ADDR(CSR_Address), .nRESET(nRESET), .CSR_OUT(CSR_IN), .mie(out_33),
    .MEI1E(mie_1_mei1e), .MEI2E(mie_1_mei2e), .MEI3E(mie_1_mei3e));
  MIP mip_1 (
    .CLK(CLK), .BUS_CLK(BUS_CLK), .CSR_IN(CSR_OUT), .CSR_IN_LATCH(CSR_IN_LATCH),
    .CSR_OUT_LATCH(CSR_OUT_LATCH), .CSR_ADDR(CSR_Address), .nINT1(nKB_INT), .nINT2(button_1_out),
    .nINT3(button_2_out), .nRESET(nRESET), .CSR_OUT(CSR_IN), .mip(out_34), .MEI1P(mip_1_mei1p),
    .MEI2P(mip_1_mei2p), .MEI3P(mip_1_mei3p));
  MCAUSE mcause_1 (
    .BUS_CLK(BUS_CLK), .CSR_IN_LATCH(CSR_IN_LATCH), .CSR_OUT_LATCH(CSR_OUT_LATCH), .CSR_ADDR(CSR_Address),
    .TRAP2(TRAP2), .nIRQ(nIRQ), .INT1P(INT1P), .INT2P(INT2P), .INT3P(INT3P), .IRQ_LATCH(d_ff_as_2_q),
    .nRESET(nRESET), .CSR_OUT(CSR_IN), .mcause(out_35));
  and and_3 (and_3_out, nRESET, nOPDONE);
  CSR csr_1 (
    .CLK(BUS_CLK), .INA(multiplexer_1_out), .INB(CSR_IN), .CSR_FUNC(out_10[12:11]), .ADDR_IN(ImmI),
    .ADDR_LATCH(CSR_ADDR_LATCH), .nRESET(nRESET), .NEW_VAL(CSR_OUT), .ADDR(CSR_Address));
  // Interrupt_Controller interrupt_controller_1: pin names not known; wires that end beside it: BUS_CLK, TRAP_OP_SnP, LASTSTEP, and_2_out, OP_LATCH, nRESET, TRAP_OP, OP_IN_MUX
  D_FF #(.Default(1)) d_ff_1 (.D(comparator_1_lt), .C(~nOPDONE), .Q(d_ff_1_q));  // open: nQ
  D_FF #(.Default(1)) d_ff_2 (.D(comparator_2_eq), .C(~nOPDONE), .nQ(BR_STOP));  // open: Q
  DebugShift32 debugshift32_1 (.CLK(BUS_CLK), .D(ALU_A), .nEN(1'b0), .Val(A));
  DebugShift32 debugshift32_2 (.CLK(BUS_CLK), .D(ALU_B), .nEN(1'b0), .Val(B));
  DebugShift32 debugshift32_3 (.CLK(BUS_CLK), .D(ADDR_IN), .nEN(1'b0), .Val(Result));
  DiodeBackward diodebackward_1 (.in(d_ff_1_q), .out(B_STOP));
  DiodeBackward diodebackward_2 (.in(BUT_STOP), .out(B_STOP));
  DiodeBackward diodebackward_3 (.in(BR_STOP), .out(B_STOP));
  D_FF_AS d_ff_as_3 (.Set(~1'b1), .D(1'b1), .C(ADDR_LATCH), .Clr(~and_3_out), .Q(TRAP_OP_SnP));  // open: nQ
  PullUp pullup_1 (.out(B_STOP));
  not not_3 (not_3_out, TRAP2[0]);
  and and_4 (INT1P, mie_1_mei1e, mip_1_mei1p);
  and and_5 (INT2P, mie_1_mei2e, mip_1_mei2p);
  and and_6 (INT3P, mie_1_mei3e, mip_1_mei3p);
  and and_7 (MRET, not_3_out, TRAP2[1]);
  Reset reset_1 (.out(nRESET));
  Reset #(.invertOutput("false")) reset_2 (.out(RESET));
  Multiplexer multiplexer_2 (.sel(MRET), .in_0(MTVEC_OUT), .in_1(MEPC_OUT), .out(CSR_PC_OUT));
  DiodeForward diodeforward_1 (.in(INT1P), .out(diodeforward_1_out));
  DiodeForward diodeforward_2 (.in(INT2P), .out(diodeforward_1_out));
  DiodeForward diodeforward_3 (.in(INT3P), .out(diodeforward_1_out));
  Multiplexer multiplexer_3 (.sel(PC_IN_MUX), .in_0(ADDR_IN), .in_1(CSR_PC_OUT), .out(PC_IN));
  not not_4 (nPC_CNT_PE, PC_IN_LATCH);
  Multiplexer multiplexer_4 (.sel(OP_IN_MUX), .in_0(MEM_OUT), .in_1(TRAP_OP), .out(OP_IN));
  D_FF d_ff_3 (.D(OP_LATCH), .C(CLK), .Q(OP_IMM_LATCH));  // open: nQ
  not not_5 (nWAKEUP, diodeforward_1_out);
  PullDown pulldown_3 (.out(diodeforward_1_out));
  Multiplexer #(.Selector_Bits(2)) multiplexer_5 (
    .sel(ALU_A_MUX), .in_0(RS1), .in_1(PC_OUT), .in_2(1'b1), .in_3(1'b0), .out(ALU_A));
  D_FF d_ff_4 (.D(ALU_AUX), .C(CLK), .Q(d_ff_4_q));  // open: nQ
  nand nand_1 (nIRQ, MIE, diodeforward_1_out);
  Clock_driver clock_driver_1 (
    .CLK_RAW(CLK_RAW), .Stop(B_STOP), .Run(B_RUN), .One_Instruction(B_INSTR), .One_Step(B_STEP),
    .One_Substep(B_SUBSTEP), .nSTEPDONE(nSTEPDONE), .nOPDONE(nOPDONE), .nRESET(nRESET), .nWAKEUP(nWAKEUP),
    .SLEEP(SLEEP), .CLK(CLK), .nCLK(nCLK), .LED_R(Running));  // open: nWAIT, LED_G
  or or_1 (or_1_out, nSTEPDONE, d_ff_4_q);
  nand nand_2 (LEN8, LEN[0], BUS_EN);
  // ALU_shift_step alu_shift_step_1: pin names not known; wires that end beside it: nCLK, nALU_RESET, or_1_out, alu_shift_step_1_p4, alu_shift_step_1_p5, alu_shift_step_1_p6
  PC pc_1 (
    .CLK(CLK), .BUS_CLK(BUS_CLK), .IN(PC_IN), .IN_LATCH(PC_IN_LATCH), .OUT_LATCH(PC_OUT_LATCH),
    .OUT_SnP(PC_OUT_SnP), .CNT_EN(nPC_CNT_PE), .CNT_2(OP_LATCH), .nRESET(nRESET), .OUT(PC_OUT), .PC(PC));
  and and_8 (PC_OUT_LATCH, nILL_OP, LASTSTEP);
  // OpCode opcode_1: pin names not known; wires that end beside it: BUS_CLK, OP_IN, OP_LATCH, OP_IMM_LATCH, BUS_EN, nRESET, ImmI, ImmS, ImmB, ImmU, ImmJ, ImmCSR, RSA, RSB, RSD, out_10[10:6], out_10[13:11], out_10[14], nS_EXT, out_10[16], TRAP2, Instr, out_11
  Multiplexer #(.Selector_Bits(3)) multiplexer_6 (
    .sel(ALU_B_MUX), .in_0(MEM_IN), .in_1(ImmI), .in_2(ImmS), .in_3(ImmB), .in_4(ImmU), .in_5(ImmJ),
    .in_6(1'b1), .in_7(1'b0), .out(ALU_B));
  nor nor_1 (LASTSTEP, LEN[0], BUS_EN);
  Clock clock_1 (
    .CLK(CLK), .nCLK(nCLK), .LEN8(LEN8), .LASTSTEP(LASTSTEP), .nRESET(nRESET), .STEP(out_10[5:0]),
    .LASTSUBSTEP(clock_1_lastsubstep), .nSTEPDONE(nSTEPDONE), .SUBSTEP(Substep), .nOPDONE(nOPDONE));
  // ALU alu_1: pin names not known; wires that end beside it: BUS_CLK, ALU_A, ALU_B, ALU_N, nALU_RESET, ALU_AUX, ALU_OP, alu_shift_step_1_p4, alu_shift_step_1_p5, alu_shift_step_1_p6, out_10[15], ADDR_IN, out_29
  Multiplexer #(.Selector_Bits(2)) multiplexer_7 (
    .sel(REG_IN_MUX), .in_0(ADDR_IN), .in_1(MEM_OUT), .in_2(CSR_IN), .in_3(PC_OUT), .out(REG_IN));
  and and_9 (BUS_CLK, CLK, BUS_EN);
  Mem mem_1 (
    .CLK(CLK), .IN(BUS_CLK), .LATCH_IN(MEM_IN), .LATCH_OUT(ADDR_IN), .SnP_OUT(ADDR_LATCH),
    .ADDR_IN(ADDR_CLK), .LATCH_ADDR(nADDR_PE), .CLK_ADDR(nMEM_OE), .nPE_ADDR(nMEM_WE), .nRESET(nS_EXT),
    .nOE(nRESET));  // open: nWE, OUT
  Terminal terminal_1 (.A(DATA_ADDR), .nCS(CS_IO), .nWE(nMEM_WE), .nOE(nMEM_OE), .D(DATA), .nINT(nKB_INT));
  Register_bank register_bank_1 (
    .CLK(BUS_CLK), .IN(REG_IN), .nEN_IN(nREG_IN_EN), .SA(RSA), .SB(RSB), .SD(RSD), .RESET(RESET), .A(RS1),
    .B(MEM_IN));
  EEPROM #(.AddrBits(16), .Bits(8)) Firmware (.A(DATA_ADDR), .CS(~CS_ROM), .WE(~nMEM_WE), .OE(~nMEM_OE), .D(DATA));
  RAMSinglePortSel #(.AddrBits(16), .Bits(8)) RAM (.A(DATA_ADDR), .CS(~CS_RAM), .WE(~nMEM_WE), .OE(~nMEM_OE), .D(DATA));
  D_FF #(.Bits(8)) d_ff_5 (.D(DATA), .C(nMEM_OE), .Q(Data_Read));  // open: nQ
  D_FF #(.Bits(8)) d_ff_6 (.D(DATA), .C(nMEM_WE), .Q(Data_Write));  // open: nQ
  ROM #(.AddrBits(17), .isProgramMemory("true"), .Bits(32)) MicroCode (
    .A(out_10), .sel(1'b1),
    .D({MicroCode_d, SLEEP, PC_IN_MUX, CSR_IN_LATCH, CSR_OUT_LATCH, CSR_ADDR_LATCH, OP_LATCH, REG_IN_MUX, ALU_B_MUX, ALU_A_MUX, nMEM_WE, nMEM_OE, nADDR_PE, ADDR_CLK, ADDR_LATCH, PC_OUT_SnP, PC_IN_LATCH, nREG_IN_EN, BUS_EN, LEN[0], ALU_OP, ALU_AUX, nALU_RESET, ALU_N}));
  D_FF #(.Default(1)) d_ff_7 (.D(MicroCode_d[29]), .C(CLK), .Q(nILL_OP));  // open: nQ

  assign out_36 = out_10[16:6];
  assign Step = out_10[5:0];

  // Other names for the same wires on the sheet: IMM_SnP = BUS_EN; LEN[1] = BUS_EN; PC_CNT_EN = OP_LATCH;
  //   ALU_OUT = ADDR_IN; CSR_ADDR[11:0] = CSR_Address; FLAG = out_10[15]; FUNC3[2:0] = out_10[13:11];
  //   gp[31:0] = x3_gp; Mem_Addr[31:0] = Address; Mem_Data_R[7:0] = Data_Read; Mem_Data_W[7:0] = Data_Write;
  //   OPCODE[4:0] = out_10[10:6]; RS2 = MEM_IN; SA = out_10[14]; SYS = out_10[16]

  // Notes on the sheet:
  //   CLK_RAW: Hz: 50000
  //   Debug
  //   Interrupts
  //   CSR
  //   Clock
  //   ALU
  //   PC
  //   Opcode
  //   Registers
  //   Memory
  //   contents of Firmware (hex, n*v repeats v):
  //   17,1,1,0,13,1,1,0,97,31,0,0,93,81,41,35,73,70,4,30,b7,7,2,0,73,a0,47,30,97,7,0,0,
  //   93,87,7,1,73,90,57,30,6f,0,40,1a,13,1,81,ff,23,20,61,0,23,22,71,0,73,23,20,34,63,
  //   40,3,8,93,3,20,0,63,c,73,0,93,3,30,0,63,a,73,0,93,3,b0,0,63,8,73,0,6f,0,0,0,6f,0,
  //   0,0,6f,0,0,0,73,23,10,34,13,3,43,0,73,10,13,34,13,3,0,4,63,88,62,0,13,3,60,d,63,86,
  //   62,2,6f,0,40,3,13,5,0,0,93,82,5,0,37,3,0,c0,63,8,c5,2,83,c3,2,0,23,0,73,0,93,82,12,
  //   0,13,5,15,0,6f,f0,df,fe,63,14,5,0,13,85,c1,95,6f,0,0,1,13,5,f0,ff,6f,0,80,0,6f,0,
  //   0,0,83,23,41,0,3,23,1,0,13,1,81,0,73,0,20,30,13,1,81,ff,23,20,f1,0,23,22,e1,0,f3,
  //   27,20,34,63,c4,7,2,13,7,30,0,63,8c,e7,0,13,7,b0,0,63,8a,e7,0,13,7,20,0,63,98,e7,0,
  //   6f,0,0,0,6f,0,0,0,93,87,2,0,3,27,41,0,83,27,1,0,13,1,81,0,73,0,20,30,37,37,0,0,73,
  //   0,50,10,83,27,c7,b5,3,c5,7,0,13,75,f5,f,e3,8,5,fe,b7,7,2,0,73,b0,47,34,67,80,0,0,
  //   b7,37,0,0,83,a7,7,b6,23,80,a7,0,67,80,0,0,37,37,0,0,83,47,5,0,63,94,7,0,67,80,0,0,
  //   83,26,7,b6,13,5,15,0,23,80,f6,0,6f,f0,9f,fe,13,1,41,ff,23,22,81,0,23,20,91,0,23,24,
  //   11,0,13,4,0,0,93,84,c1,80,ef,f0,5f,f9,13,7,a0,0,63,14,e5,2,33,84,84,0,23,0,4,0,83,
  //   20,81,0,3,24,41,0,a3,8f,4,0,13,85,c1,80,83,24,1,0,13,1,c1,0,67,80,0,0,33,87,84,0,
  //   23,0,a7,0,13,4,14,0,13,7,f0,1,e3,10,e4,fc,6f,f0,1f,fd,13,1,41,ff,13,6,30,0,93,85,
  //   c1,83,13,5,0,0,23,24,11,0,23,22,81,0,ef,0,0,25,13,85,1,84,ef,0,c0,23,13,85,c1,84,
  //   ef,f0,9f,f5,ef,f0,5f,f7,93,5,5,0,13,85,1,86,ef,0,c0,7,37,34,0,0,ef,f0,df,f0,83,27,
  //   4,b6,23,80,a7,0,6f,f0,5f,ff,13,1,1,fe,23,24,81,0,23,22,91,0,23,26,11,0,23,28,c1,0,
  //   23,2a,d1,0,23,2c,e1,0,23,2e,f1,0,13,4,5,0,93,84,5,0,63,8,5,0,83,27,85,1,63,94,7,0,
  //   ef,0,90,d,83,25,84,0,93,6,1,1,13,86,4,0,13,5,4,0,23,20,d1,0,ef,10,40,a,83,20,c1,0,
  //   3,24,81,0,83,24,41,0,13,1,1,2,67,80,0,0,13,1,81,fd,23,22,f1,2,23,26,81,0,13,4,5,0,
  //   3,a5,81,80,23,28,11,0,23,2a,b1,0,23,2c,c1,0,23,2e,d1,0,23,20,e1,2,63,c,5,0,83,27,
  //   85,1,63,98,7,0,23,20,a1,0,ef,0,10,7,3,25,1,0,83,25,85,0,93,6,41,1,13,6,4,0,23,22,
  //   d1,0,ef,10,c0,3,83,20,1,1,3,24,c1,0,13,1,81,2,67,80,0,0,13,1,1,ff,23,22,91,0,23,26,
  //   11,0,23,24,81,0,23,20,b1,0,93,4,5,0,63,8,5,0,3,27,85,1,63,14,7,0,ef,0,10,2,3,a7,84,
  //   1,3,a4,84,0,63,16,7,0,13,85,4,0,ef,0,d0,0,13,87,81,88,63,12,e4,4,3,a4,44,0,3,57,c4,
  //   0,13,77,87,0,63,6,7,0,3,27,4,1,63,10,7,8,93,5,4,0,13,85,4,0,ef,0,c0,29,63,8,5,6,13,
  //   5,f0,ff,83,20,c1,0,3,24,81,0,83,24,41,0,13,1,1,1,67,80,0,0,13,87,81,8a,63,16,e4,0,
  //   3,a4,84,0,6f,f0,9f,fb,13,87,81,86,e3,18,e4,fa,3,a4,c4,0,6f,f0,9f,fa,83,27,1,0,23,
  //   24,e4,0,93,87,17,0,23,20,f1,0,63,5a,7,0,83,26,84,1,63,4c,d7,4,13,7,a0,0,63,88,e5,
  //   4,3,27,4,0,93,6,17,0,23,20,d4,0,23,0,b7,0,83,27,1,0,3,27,84,0,83,c5,7,0,13,7,f7,ff,
  //   e3,9e,5,fa,23,24,e4,0,63,5e,7,2,13,6,4,0,93,5,a0,0,13,85,4,0,ef,0,40,6,93,7,f0,ff,
  //   e3,2,f5,f6,13,5,a0,0,6f,f0,1f,f6,13,6,4,0,13,85,4,0,ef,0,80,4,13,7,f0,ff,e3,1a,e5,
  //   fa,6f,f0,5f,f4,83,27,4,0,13,87,17,0,23,20,e4,0,13,7,a0,0,23,80,e7,0,6f,f0,df,fc,93,
  //   5,5,0,3,a5,81,80,6f,f0,5f,eb,93,6,6,0,13,86,5,0,93,5,5,0,3,a5,81,80,6f,0,0,15,13,
  //   1,c1,fe,23,26,81,0,23,24,91,0,23,28,11,0,93,7,5,0,93,84,5,0,13,4,6,0,63,c,5,0,3,27,
  //   85,1,63,18,7,0,23,20,a1,0,ef,0,40,6b,83,27,1,0,13,87,81,88,63,12,e4,c,3,a4,47,0,3,
  //   27,84,1,23,24,e4,0,3,57,c4,0,13,77,87,0,63,6,7,c,3,27,4,1,63,2,7,c,3,27,4,1,3,25,
  //   4,0,93,f6,f4,f,93,f4,f4,f,33,5,e5,40,3,27,44,1,63,42,e5,2,13,85,7,0,93,5,4,0,23,22,
  //   d1,0,23,20,f1,0,ef,0,40,48,83,27,1,0,83,26,41,0,63,10,5,a,3,27,84,0,13,5,15,0,13,
  //   7,f7,ff,23,24,e4,0,3,27,4,0,13,6,17,0,23,20,c4,0,23,0,d7,0,3,27,44,1,63,c,a7,0,3,
  //   57,c4,0,13,77,17,0,63,e,7,0,13,7,a0,0,63,9a,e4,0,93,5,4,0,13,85,7,0,ef,0,0,43,63,
  //   1a,5,4,83,20,1,1,3,24,c1,0,13,85,4,0,83,24,81,0,13,1,41,1,67,80,0,0,13,87,81,8a,63,
  //   16,e4,0,3,a4,87,0,6f,f0,9f,f3,13,87,81,86,e3,18,e4,f2,3,a4,c7,0,6f,f0,9f,f2,13,85,
  //   7,0,93,5,4,0,23,20,f1,0,ef,0,40,7,83,27,1,0,e3,6,5,f2,93,4,f0,ff,6f,f0,df,fa,13,86,
  //   5,0,93,5,5,0,3,a5,81,80,6f,f0,9f,eb,13,1,41,ff,23,22,81,0,23,20,91,0,13,4,5,0,13,
  //   85,5,0,93,5,6,0,13,86,6,0,23,24,11,0,23,a6,1,82,ef,20,c0,46,93,7,f0,ff,63,18,f5,0,
  //   83,a7,c1,82,63,84,7,0,23,20,f4,0,83,20,81,0,3,24,41,0,83,24,1,0,13,1,c1,0,67,80,0,
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  //   Microcode
  //   contents of MicroCode (hex, n*v repeats v):
  //   1d1c0a8a,190202,130202,1d0242,170202,1d0242,170202,1d0242,170202,1d0242,3d0202,1d0200,
  //   41c0282,190202,130202,201d0042,201d0042,201d0042,201d0042,201d0102,0,0,0,0,0,0,0,
  //   0,0,0,0,0,1d1c0a8a,190202,130202,1d0242,170202,1d0242,170202,1d0242,170202,1d0242,
  //   3d0202,3d0202,3d0202,3d0302,0,0,0,0,0,0,0,0,0,0,0,0,0,0,0,0,0,0,1d1c0a8a,190202,130202,
  //   1d0242,170202,1d0242,170202,1d0242,170202,1d0242,3d0202,3d0202,3d0202,3d0302,0,0,
  //   0,0,0,0,0,0,0,0,0,0,0,0,0,0,0,0,1d1c0a8a,190202,130202,1d0242,170202,1d0242,170202,
  //   1d0242,170202,1d0242,3d0202,3d0202,3d0202,3d0302,0,0,0,0,0,0,0,0,0,0,0,0,0,0,0,0,
  //   0,0,1d1c0a8a,190202,130202,1d0242,170202,1d0242,170202,1d0242,170202,1d0242,3d0202,
  //   1d0200,41d0082,1d0302,0,0,0,0,0,0,0,0,0,0,0,0,0,0,0,0,0,0,1d1c0a8a,190202,130202,
  //   1d0242,170202,1d0242,170202,1d0242,170202,1d0242,3d0202,1d0200,111d0882,1d0302,0,
  //   0,0,0,0,0,0,0,0,0,0,0,0,0,0,0,0,0,1d1c0a8a,190202,130202,1d0242,170202,1d0242,170202,
  //   1d0242,170202,1d0242,3d0202,3d0202,3d0202,3d0302,0,0,0,0,0,0,0,0,0,0,0,0,0,0,0,0,
  //   0,0,1d1c0a8a,190202,130202,1d0242,170202,1d0242,170202,1d0242,170202,1d0242,3d0202,
  //   3d0202,3d0202,3d0302,0,0,0,0,0,0,0,0,0,0,0,0,0,0,0,0,0,0,1d1c0a8a,190202,130202,1d0242,
  //   170202,1d0242,170202,1d0242,170202,1d0242,3d0202,1d0200,81c0282,190202,1a0242,c0202,
  //   1c0302,0,0,0,0,0,0,0,0,0,0,0,0,0,0,0,1d1c0a8a,190202,130202,1d0242,170202,1d0242,
  //   170202,1d0242,170202,1d0242,3d0202,3d0202,3d0202,3d0302,0,0,0,0,0,0,0,0,0,0,0,0,0,
  //   0,0,0,0,0,1d1c0a8a,190202,130202,1d0242,170202,1d0242,170202,1d0242,170202,1d0242,
  //   3d0202,3d0202,3d0202,3d0302,0,0,0,0,0,0,0,0,0,0,0,0,0,0,0,0,0,0,1d1c0a8a,190202,130202,
  //   1d0242,170202,1d0242,170202,1d0242,170202,1d0242,3d0202,3d0202,3d0202,3d0302,0,0,
  //   0,0,0,0,0,0,0,0,0,0,0,0,0,0,0,0,1d1c0a8a,190202,130202,1d0242,170202,1d0242,170202,
  //   1d0242,170202,1d0242,3d0202,1d0200,1d0082,1d0302,0,0,0,0,0,0,0,0,0,0,0,0,0,0,0,0,
  //   0,0,1d1c0a8a,190202,130202,1d0242,170202,1d0242,170202,1d0242,170202,1d0242,3d0202,
  //   1d0200,131d0082,1d0302,0,0,0,0,0,0,0,0,0,0,0,0,0,0,0,0,0,0,1d1c0a8a,190202,130202,
  //   1d0242,170202,1d0242,170202,1d0242,170202,1d0242,3d0202,3d0202,3d0202,3d0302,0,0,
  //   0,0,0,0,0,0,0,0,0,0,0,0,0,0,0,0,1d1c0a8a,190202,130202,1d0242,170202,1d0242,170202,
  //   1d0242,170202,1d0242,3d0202,3d0202,3d0202,3d0302,0,0,0,0,0,0,0,0,0,0,0,0,0,0,0,0,
  //   0,0,1d1c0a8a,190202,130202,1d0242,170202,1d0242,170202,1d0242,170202,1d0242,3d0202,
  //   3d0202,3d0202,3d0302,0,0,0,0,0,0,0,0,0,0,0,0,0,0,0,0,0,0,1d1c0a8a,190202,130202,1d0242,
  //   170202,1d0242,170202,1d0242,170202,1d0242,3d0202,3d0202,3d0202,3d0302,0,0,0,0,0,0,
  //   0,0,0,0,0,0,0,0,0,0,0,0,1d1c0a8a,190202,130202,1d0242,170202,1d0242,170202,1d0242,
  //   170202,1d0242,3d0202,3d0202,3d0202,3d0302,0,0,0,0,0,0,0,0,0,0,0,0,0,0,0,0,0,0,1d1c0a8a,
  //   190202,130202,1d0242,170202,1d0242,170202,1d0242,170202,1d0242,3d0202,3d0202,3d0202,
  //   3d0302,0,0,0,0,0,0,0,0,0,0,0,0,0,0,0,0,0,0,1d1c0a8a,190202,130202,1d0242,170202,1d0242,
  //   170202,1d0242,170202,1d0242,3d0202,3d0202,3d0202,3d0302,0,0,0,0,0,0,0,0,0,0,0,0,0,
  //   0,0,0,0,0,1d1c0a8a,190202,130202,1d0242,170202,1d0242,170202,1d0242,170202,1d0242,
  //   3d0202,3d0202,3d0202,3d0302,0,0,0,0,0,0,0,0,0,0,0,0,0,0,0,0,0,0,1d1c0a8a,190202,130202,
  //   1d0242,170202,1d0242,170202,1d0242,170202,1d0242,3d0202,3d0202,3d0202,3d0302,0,0,
  //   0,0,0,0,0,0,0,0,0,0,0,0,0,0,0,0,1d1c0a8a,190202,130202,1d0242,170202,1d0242,170202,
  //   1d0242,170202,1d0242,3d0202,3d0202,3d0202,3d0302,0,0,0,0,0,0,0,0,0,0,0,0,0,0,0,0,
  //   0,0,1d1c0a8a,190202,130202,1d0242,170202,1d0242,170202,1d0242,170202,1d0242,3d0202,
  //   1d0201,1d0293,1d0206,1d0302,0,0,0,0,0,0,0,0,0,0,0,0,0,0,0,0,0,1d1c0a8a,190202,130202,
  //   1d0242,170202,1d0242,170202,1d0242,170202,1d0242,3d0202,1d0200,41d0282,1d0600,1d1d08c2,
  //   1d1d0202,191d08c2,191d08c2,191d08c2,191d0842,191d0842,191d0842,1d0302,0,0,0,0,0,0,
  //   0,0,0,1d1c0a8a,190202,130202,1d0242,170202,1d0242,170202,1d0242,170202,1d0242,3d0202,
  //   3d0202,3d0202,3d0302,0,0,0,0,0,0,0,0,0,0,0,0,0,0,0,0,0,0,1d1c0a8a,190202,130202,1d0242,
  //   170202,1d0242,170202,1d0242,170202,1d0242,3d0202,1d0200,151d0a82,1d0600,1d1d08c2,
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endmodule
